# Fritzing sketch foos_RPi_only (saved by Fritzing 0.9.3b)
breadboards: 1

parts:
  Raspberry_Pi_1 = Raspberry Pi 3 [part_number=RPI-3-V1.2]
  Q1 = PNP-Transistor [package="TO92 [THT]"]
  R2 = Resistor [tolerance=±5% resistance=330 package="0805 [SMD]"]
  IR1 = TSOP312.., 314.. [package=THT]
  R1 = Resistor [tolerance=±5% resistance=10k package="0805 [SMD]"]
  R3 = Resistor [tolerance=±5% resistance=330 package="0805 [SMD]"]
  LED1 = smd LED [color="Infrared (940nm)" package="1206 [SMD]"]
  LED2 = smd LED [color="Infrared (940nm)" package="1206 [SMD]"]
  IR2 = TSOP312.., 314.. [package=THT]
  Yellow+ = SWITCH-MOMENTARY-2 [package=tactile-pth-12mm]
  Yellow- = SWITCH-MOMENTARY-2 [package=tactile-pth-12mm]
  Black- = SWITCH-MOMENTARY-2 [package=tactile-pth-12mm]
  Black+ = SWITCH-MOMENTARY-2 [package=tactile-pth-12mm]
  Ok = SWITCH-MOMENTARY-2 [package=tactile-pth-12mm]

nets:
  N1: Raspberry_Pi_1.GPIO2, Black+.2
  GND: Raspberry_Pi_1.GND, IR1.GND, LED1.cathode, LED2.cathode, IR2.GND, Yellow+.2, Yellow-.2, Black-.2, Black+.1, Ok.2
  N2: Raspberry_Pi_1.GPIO7, IR1.Data
  N3: Raspberry_Pi_1.GPIO8, Ok.1
  N4: Raspberry_Pi_1.GPIO25, Black-.1
  N5: Raspberry_Pi_1.GPIO23, Yellow-.1
  N6: Raspberry_Pi_1.GPIO18, R1.Pin_1
  N7: Raspberry_Pi_1.GPIO15, Yellow+.1
  N8: Raspberry_Pi_1.GPIO14, IR2.Data
  N9: Raspberry_Pi_1.5V, Q1.E, IR1.Vs, IR2.Vs
  N10: Q1.B, R1.Pin_0
  N11: Q1.C, R2.Pin_0, R3.Pin_0
  N12: R2.Pin_1, LED1.anode
  N13: R3.Pin_1, LED2.anode
